# Fritzing sketch FritzingSketch (saved by Fritzing 1.0.5)
breadboards: 2

parts:
  LCD1 = LCD screen
  Nano = Arduino Nano (Rev3.0)
  S1 = Pushbutton [package="[SMD]"]
  S2 = Pushbutton [package="[SMD]"]
  S4 = Pushbutton [package="[SMD]"]
  SP1 = SPEAKER [package=pcb_mount_speaker]
  DFRobot_DFPlayer_Mini1 = DFRobot DFPlayer Mini [part_number=DFR0299]
  S3 = Pushbutton [package="[SMD]"]
  Q1 = NPN-Transistor [package="TO92 [THT]"]
  R1 = Resistor [tolerance=±5% power=0.25W resistance=1k package=THT]
  R2 = Resistor [tolerance=±5% power=0.25W resistance=10k package=THT]
  Деталь1 = TRRS 3.5mm Jack Breakout
  LCM1602_IIC1 = LCM1602 IIC [part_number="LCM1602 IIC" chip_label="LCM1602 IIC" package="DIP (Dual Inline) [THT]"]
  C1 = Electrolytic Capacitor [capacitance=0.47mF voltage=20V package="0807 [SMD, electrolytic]"]

nets (from the schematic view):
  VSS: LCD1.VSS, LCM1602_IIC1.VSS
  VDD: LCD1.VDD, LCM1602_IIC1.VDD
  N1: LCD1.V0, LCM1602_IIC1.V0
  N2: LCD1.RS, LCM1602_IIC1.RS
  N3: LCD1.R/W, LCM1602_IIC1.RW
  N4: LCD1.E, LCM1602_IIC1.E
  N5: LCD1.DB0, LCM1602_IIC1.D0
  N6: LCD1.DB1, LCM1602_IIC1.D1
  N7: LCD1.DB2, LCM1602_IIC1.D2
  N8: LCD1.DB3, LCM1602_IIC1.D3
  N9: LCD1.DB4, LCM1602_IIC1.D4
  N10: LCD1.DB5, LCM1602_IIC1.D5
  N11: LCD1.DB6, LCM1602_IIC1.D6
  N12: LCD1.DB7, LCM1602_IIC1.D7
  N13: LCD1.LED+, LCM1602_IIC1.A
  N14: LCD1.LED-, LCM1602_IIC1.K
  GND: Nano.GND, S1.Pin_3, S1.Pin_4, S2.Pin_3, S2.Pin_4, S4.Pin_3, S4.Pin_4, DFRobot_DFPlayer_Mini1.GND-1, DFRobot_DFPlayer_Mini1.GND-2, S3.Pin_3, S3.Pin_4, Деталь1.SLEEVE, Деталь1.RING2, LCM1602_IIC1.GND, C1.-
  N15: Nano.D2, S1.Pin_1, S1.Pin_2
  N16: Nano.D3, S2.Pin_1, S2.Pin_2
  N17: Nano.D4, S3.Pin_1, S3.Pin_2
  N18: Nano.D6, S4.Pin_1, S4.Pin_2
  N19: Nano.D7, DFRobot_DFPlayer_Mini1.BUSY
  N20: Nano.D8, DFRobot_DFPlayer_Mini1.DAC_L, Деталь1.TIP
  N21: Nano.D9, R2.Pin_1
  N22: Nano.D10, DFRobot_DFPlayer_Mini1.TX
  N23: Nano.D11/MOSI, R1.Pin_0
  VCC: Nano.5V, DFRobot_DFPlayer_Mini1.VCC, LCM1602_IIC1.VCC, C1.+
  N24: Nano.A5, LCM1602_IIC1.SCL
  N25: Nano.A4, LCM1602_IIC1.SDA
  N26: SP1.+, DFRobot_DFPlayer_Mini1.SPK_2
  N27: SP1.-, Q1.E
  N28: DFRobot_DFPlayer_Mini1.RX, R1.Pin_1
  N29: DFRobot_DFPlayer_Mini1.DAC_R, Деталь1.RING1
  N30: DFRobot_DFPlayer_Mini1.SPK_1, Q1.C
  N31: Q1.B, R2.Pin_0

custom parts:
  LCM1602 IIC: I2C-Module to use a 1602 or 2004 LCD on with the wire.h libory Serial LCD Modul

// code stored in the sketch: DanilOS.ino
#include <Wire.h>
#include <LiquidCrystal_I2C.h>
#include "screen_logo.h"
#include "screen_mp3.h"
#include "screen_menu.h"

LiquidCrystal_I2C lcd(0x27, 16, 2);
DanilScreen currentScreen = SCREEN_BOOT;

void setup() {
  lcd.begin();
  lcd.backlight();

  pinMode(2, INPUT_PULLUP); // prev
  pinMode(3, INPUT_PULLUP); // next
  pinMode(4, INPUT_PULLUP); // play/pause / enter
  pinMode(5, INPUT_PULLUP); // back
  pinMode(6, INPUT_PULLUP); // fn

  showSquirrelLogo(lcd);
  currentScreen = SCREEN_MENU;
}

void loop() {
  if (!digitalRead(5)) {
    currentScreen = SCREEN_MENU;
    delay(250);
  }

  switch (currentScreen) {
    case SCREEN_MENU:
      updateMenu(lcd, currentScreen);
      break;
    case SCREEN_MP3:
      updateScreenMP3(lcd);
      break;
  }
}
