# Fritzing sketch FritzingSketch (saved by Fritzing 1.0.5)
breadboards: 2

parts:
  LCD1 = LCD screen
  Nano = Arduino Nano (Rev3.0)
  S1 = Pushbutton [package="[SMD]"]
  S2 = Pushbutton [package="[SMD]"]
  S4 = Pushbutton [package="[SMD]"]
  SP1 = SPEAKER [package=pcb_mount_speaker]
  LCM1602_IIC1 = generic_ic_dip_22_300mil.fzp [part_number="LCM1602 IIC" chip_label="LCM1602 IIC"]
  DFRobot_DFPlayer_Mini1 = DFRobot DFPlayer Mini [part_number=DFR0299]
  S3 = Pushbutton [package="[SMD]"]

nets (from the schematic view):
  N1: LCD1.VSS, LCM1602_IIC1.connector0
  N2: LCD1.VDD, LCM1602_IIC1.connector1
  N3: LCD1.V0, LCM1602_IIC1.connector2
  N4: LCD1.RS, LCM1602_IIC1.connector3
  N5: LCD1.R/W, LCM1602_IIC1.connector4
  N6: LCD1.E, LCM1602_IIC1.connector5
  N7: LCD1.DB0, LCM1602_IIC1.connector6
  N8: LCD1.DB1, LCM1602_IIC1.connector7
  N9: LCD1.DB2, LCM1602_IIC1.connector8
  N10: LCD1.DB3, LCM1602_IIC1.connector9
  N11: LCD1.DB4, LCM1602_IIC1.connector10
  N12: LCD1.DB5, LCM1602_IIC1.connector11
  N13: LCD1.DB6, LCM1602_IIC1.connector12
  N14: LCD1.DB7, LCM1602_IIC1.connector13
  N15: LCD1.LED+, LCM1602_IIC1.connector14
  N16: LCD1.LED-, LCM1602_IIC1.connector15
  N17: Nano.GND, S1.Pin_3, S1.Pin_4, S2.Pin_3, S2.Pin_4, S4.Pin_3, S4.Pin_4, LCM1602_IIC1.connector16, DFRobot_DFPlayer_Mini1.GND-1, DFRobot_DFPlayer_Mini1.GND-2, S3.Pin_3, S3.Pin_4
  N18: Nano.D2, S1.Pin_1, S1.Pin_2
  N19: Nano.D3, S2.Pin_1, S2.Pin_2
  N20: Nano.D4, S3.Pin_1, S3.Pin_2
  N21: Nano.D6, S4.Pin_1, S4.Pin_2
  N22: Nano.D7, DFRobot_DFPlayer_Mini1.BUSY
  N23: Nano.D10, DFRobot_DFPlayer_Mini1.TX
  N24: Nano.D11/MOSI, DFRobot_DFPlayer_Mini1.RX
  5V: Nano.5V, LCM1602_IIC1.connector17, DFRobot_DFPlayer_Mini1.VCC
  N25: Nano.A5, LCM1602_IIC1.connector19
  N26: Nano.A4, LCM1602_IIC1.connector18
  N27: SP1.+, DFRobot_DFPlayer_Mini1.SPK_2
  N28: SP1.-, DFRobot_DFPlayer_Mini1.SPK_1

// code stored in the sketch: DanilOS.ino
#include <Wire.h>
#include <LiquidCrystal_I2C.h>
#include "screen_logo.h"
#include "screen_mp3.h"
#include "screen_menu.h"

LiquidCrystal_I2C lcd(0x27, 16, 2);
DanilScreen currentScreen = SCREEN_BOOT;

void setup() {
  lcd.begin();
  lcd.backlight();

  pinMode(2, INPUT_PULLUP); // prev
  pinMode(3, INPUT_PULLUP); // next
  pinMode(4, INPUT_PULLUP); // play/pause / enter
  pinMode(5, INPUT_PULLUP); // back
  pinMode(6, INPUT_PULLUP); // fn

  showSquirrelLogo(lcd);
  currentScreen = SCREEN_MENU;
}

void loop() {
  if (!digitalRead(5)) {
    currentScreen = SCREEN_MENU;
    delay(250);
  }

  switch (currentScreen) {
    case SCREEN_MENU:
      updateMenu(lcd, currentScreen);
      break;
    case SCREEN_MP3:
      updateScreenMP3(lcd);
      break;
  }
}
